# Fritzing sketch Smart_Weather_Monitoring_System (saved by Fritzing 0.9.3b)
breadboards: 1

parts:
  U2 = LCD-16X2 [package=lcd-16x2_noholes]
  U3 = POT [package=pot_mammoth]
  DHT1 = DHT11 Humitidy and Temperature Sensor
  U1 = NodeMCU V1.0

nets:
  GND: U2.VSS, U2.R_W, U2.K, U3.E, DHT1.GND, U1.GND
  VDD: U2.VDD, U2.A, U3.S, U1.Vin
  N1: U2.VO, U3.A
  N2: U2.RS, U1.D1
  N3: U2.E, U1.D2
  N4: U2.DB4, U1.D3
  N5: U2.DB5, U1.D4
  N6: U2.DB6, U1.D5
  N7: U2.DB7, U1.D6
  VDD_2: DHT1.VDD, U1.3V3
  N8: DHT1.DATA, U1.D7

custom parts:
  DHT11 Humitidy and Temperature Sensor: DHT11 Humidity and Temperature Sensor
  NodeMCU V1.0: ESP8266 based NodeMCU
